# Fritzing sketch pn532wiring (saved by Fritzing 0.9.3b)
breadboards: 1

parts:
  Part1 = Adafruit PN532 Breakout [part_number="Adafruit #364"]
  Part2 = Arduino Nano (Rev3.0)

nets:
  GND: Part1.SEL0, Part1.GND, Part2.GND
  VDD: Part1.VDD, Part1.SEL1, Part2.VIN
  N1: Part1.SCK, Part2.D13/SCK
  N2: Part1.MISO, Part2.D12/MISO
  N3: Part1.MOSI/SDA/TX, Part2.D11/MOSI
  N4: Part1.NSS/SCL/RX, Part2.D10

custom parts:
  Adafruit PN532 Breakout: The PN532 is the most popular NFC chip, and is what is embedded in pretty much every phone or device that does NFC. It can pretty much do it all, such as read and write to tags and cards, communicate with phones (say for payment processing), and 'act' like a NFC tag. If you want to do any sort of embedded NFC work, this is the chip you'll want to use! NFC (Near Field Communications) is a way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
